# Fritzing sketch Relay (saved by Fritzing 0.9.3b)
breadboards: 1

parts:
  Часть1 = Arduino Uno (Rev3)
  S1 = Pushbutton [package="[THT]"]
  RelayINPUT1 = Relay Shield INPUT [chip_label=? package=THT]
  RelayOUTPUT1 = Relay Shield OUTPUT [chip_label=? package=THT]
  J1 = Camdenboss CTB0158-4 [part_number=CTB0158-4 package=THT]

nets:
  N1: Часть1.GND, S1.Pin_1, S1.Pin_2, RelayINPUT1.minus
  N2: Часть1.D2, S1.Pin_3, S1.Pin_4
  N3: Часть1.D6_PWM, RelayINPUT1.signal
  N4: Часть1.5V, RelayINPUT1.plus
  N5: RelayOUTPUT1.ground, J1.terminal_1
  N6: RelayOUTPUT1.LEDoff, J1.terminal_2
  N7: RelayOUTPUT1.LEDon, J1.terminal_3

notes:
  ВНИМАНИЕ!!!
  При прозвонке выхода реле (касании щупом тестера выходов) почти всегда возникает эффект, как будто нажата кнопка
  Все работает.
  При включении загорается светодиод L, реле находится в состоянии ОТКЛ.
  При нажатии кнопки реле инвертирует свое состояние, а светодиод гаснет на 500мс (защита от дребезга кнопки).
  После откл питания реле переходит в состояние ОТКЛ.

custom parts:
  Relay Shield INPUT: A dummy, proxy, ersatz, stand-in part for whatever you want. With 3 pins on a 100 mil inline pin header footprint.
  Relay Shield OUTPUT: A dummy, proxy, ersatz, stand-in part for whatever you want. With 3 pins on a 100 mil inline pin header footprint.

// code stored in the sketch: relay.ino

